# Fritzing sketch reaction game (saved by Fritzing 0.9.2b)
breadboards: 1

parts:
  LED1 = LED - 5mm [color="Red (633nm)" package="5 mm [THT]"]
  R1 = Resistor [tolerance=±5% resistance=220 package=THT]
  S1 = Pushbutton [package="[THT]"]
  S2 = Pushbutton [package="[THT]"]
  Raspberry_Pi1 = Raspberry Pi 2

nets:
  N1: LED1.cathode, R1.Pin_1
  N2: LED1.anode, Raspberry_Pi1.GPIO4
  N3: R1.Pin_0, S1.Pin_3, S1.Pin_4, S2.Pin_1, S2.Pin_2, Raspberry_Pi1.GND
  N4: S1.Pin_1, S1.Pin_2, Raspberry_Pi1.GPIO14
  N5: S2.Pin_3, S2.Pin_4, Raspberry_Pi1.GPIO15
