# Fritzing sketch stoplight (saved by Fritzing 0.9.2b)
breadboards: 1

parts:
  Raspberry_Pi1 = Raspberry Pi 2
  R1 = Resistor [tolerance=±5% resistance=330 package=THT]
  LED1 = LED - 5mm [color="Red (633nm)" package="5 mm [THT]"]
  LED2 = LED - 5mm [color="Green (555nm)" package="5 mm [THT]"]
  LED3 = LED - 5mm [color="Yellow (595nm)" package="5 mm [THT]"]

nets:
  N1: Raspberry_Pi1.GPIO18, LED2.anode
  N2: Raspberry_Pi1.GPIO15, LED3.anode
  N3: Raspberry_Pi1.GPIO14, LED1.anode
  N4: Raspberry_Pi1.GND, R1.Pin_0
  N5: R1.Pin_1, LED1.cathode, LED2.cathode, LED3.cathode
